# Fritzing sketch PCB-kort_klar  (saved by Fritzing 0.9.4)
circuit board: 8.84586cm x 7.61844cm
breadboards: 1

parts:
  ZS-042_RTC2 = ZS-042 RTC Module
  U2 = ESP8266 WiFi Module [part_number=ESP8266]
  Part3 = Adafruit BME680 [part_number="Adafruit #3660"]
  R1 = Resistor [tolerance=±5% resistance=1k package="1206 [SMD]"]
  R2 = Resistor [tolerance=±5% resistance=1k package="1206 [SMD]"]
  R3 = Resistor [tolerance=±5% resistance=1k package="1206 [SMD]"]
  R4 = Resistor [tolerance=±5% resistance=1k package="1206 [SMD]"]
  R7 = Resistor [tolerance=±5% resistance=1k package="1206 [SMD]"]
  R8 = Resistor [tolerance=±5% resistance=10k package="1206 [SMD]"]
  R5 = Resistor [tolerance=±5% resistance=1k package="1206 [SMD]"]
  R6 = Resistor [tolerance=±5% resistance=1k package="1206 [SMD]"]
  Part2 = Arduino Uno (Rev3) - ICSP
  J1 = female pin header, 2 pins [form="♀ (female)"]
  J2 = female pin header, 2 pins [form="♀ (female)"]
  J3 = female pin header, 2 pins [form="♀ (female)"]
  J4 = female pin header, 2 pins [form="♀ (female)"]
  J5 = female pin header, 2 pins [form="♀ (female)"]
  J6 = female pin header, 2 pins [form="♀ (female)"]
  J7 = female pin header, 2 pins [form="♀ (female)"]
  J8 = female pin header, 2 pins [form="♀ (female)"]
  J9 = female pin header, 2 pins [form="♀ (female)"]

nets:
  GND: ZS-042_RTC2.GND#6, U2.GND, Part3.GND, R5.Pin_1, Part2.GND, J4.pin2, J9.pin1
  VCC: ZS-042_RTC2.VCC, U2.VCC, Part3.VCC, R8.Pin_0, Part2.5V, Part2.3V3, J5.pin2, J8.pin1
  N1: ZS-042_RTC2.SDA, Part3.SDI/SDA, Part2.A4/SDA
  N2: ZS-042_RTC2.SCL, Part3.SCK/SCL, Part2.A5/SCL
  N3: U2.RXD, R7.Pin_1, R6.Pin_0
  N4: U2.CH_PD, R8.Pin_1
  N5: U2.TXD, Part2.D2
  N6: R1.Pin_0, Part2.D13/SCK
  N7: R1.Pin_1, J1.pin2
  N8: R2.Pin_0, Part2.ICSP_MOSI, Part2.D11_PWM/MOSI
  N9: R2.Pin_1, J3.pin2
  N10: R3.Pin_0, Part2.D10_PWM/SS
  N11: R3.Pin_1, J2.pin2
  N12: R4.Pin_0, Part2.D9_PWM
  N13: R4.Pin_1, J6.pin2
  N14: R7.Pin_0, Part2.D3_PWM
  N15: R5.Pin_0, R6.Pin_1
  N16: Part2.D5_PWM, J7.pin2

notes:
  Makerspace Flemingsberg
  Design by Amal Al-Ammari
  VCC
  GND

custom parts:
  ESP8266 WiFi Module: Generic WiFi Module based on the ESP8266 with onboard PCB antenna and UART communications
